// Logisim project 7COM1013.circ-T01L1e08.circ as structural Verilog: 1 circuit, main circuit mycircuit
module mycircuit (
  input  A,
  input  B,
  input  C,
  output R
);

  wire and_1_out;

  and and_1 (and_1_out, B, C);
  or or_1 (R, and_1_out, A);
endmodule
