// Logisim project 7COM1013.circ-T01L1e09.circ as structural Verilog: 1 circuit, main circuit mycircuit
module mycircuit (
  input  A,
  input  B,
  input  C,
  output X,
  output Y
);

  wire and_1_out, and_2_out, and_3_out, and_4_out, not_1_out, not_2_out, not_3_out, not_4_out;

  not not_1 (not_1_out, A);
  not not_2 (not_2_out, C);
  not not_3 (not_3_out, B);
  not not_4 (not_4_out, C);
  and and_1 (and_1_out, not_1_out, B, not_2_out);
  and and_2 (and_2_out, A, B, C);
  and and_3 (and_3_out, not_3_out, C);
  and and_4 (and_4_out, A, B, not_4_out);
  or or_1 (X, and_1_out, and_2_out);
  or or_2 (Y, and_3_out, and_4_out);
endmodule
