// Logisim project 7COM1013.circ-T02L1e01.circ as structural Verilog: 1 circuit, main circuit solution
module solution (
  input  [5:0] A,
  input  [5:0] B,
  output [5:0] R
);

  assign R = ~(A ^ B);  // XNOR_Gate xnor_1, 6 bits wide
endmodule
