// Logisim project 7COM1013.circ-T02L1e04.circ as structural Verilog: 2 circuits, main circuit solution
module solution (
  input  [5:0] A,
  input  [5:0] B,
  output [5:0] R,
  output C_out,
  output V
);

  wire and_1_out, and_2_out, and_3_out, and_4_out, and_5_out, and_6_out, and_7_out, and_8_out, and_9_out,
       and_10_out, and_11_out, and_12_out, not_1_out, not_2_out, not_3_out, not_4_out, not_5_out, not_6_out,
       or_1_out, or_2_out, or_3_out, or_4_out, or_5_out, xor_1_out, xor_2_out, xor_3_out, xor_4_out,
       xor_5_out, xor_6_out;

  // Probe on A
  // Probe on B
  not not_1 (not_1_out, B[0]);
  not not_2 (not_2_out, B[1]);
  not not_3 (not_3_out, B[2]);
  not not_4 (not_4_out, B[3]);
  not not_5 (not_5_out, B[4]);
  not not_6 (not_6_out, B[5]);
  xor xor_1 (xor_1_out, A[0], not_1_out);
  xor xor_2 (xor_2_out, A[1], not_2_out);
  xor xor_3 (xor_3_out, A[2], not_3_out);
  xor xor_4 (xor_4_out, A[3], not_4_out);
  xor xor_5 (xor_5_out, A[4], not_5_out);
  xor xor_6 (xor_6_out, A[5], not_6_out);
  xor xor_7 (R[0], xor_1_out, 1'b1);
  and and_1 (and_1_out, 1'b1, xor_1_out);
  and and_2 (and_2_out, A[0], not_1_out);
  xor xor_8 (R[1], xor_2_out, or_1_out);
  and and_3 (and_3_out, or_1_out, xor_2_out);
  and and_4 (and_4_out, A[1], not_2_out);
  xor xor_9 (R[2], xor_3_out, or_2_out);
  and and_5 (and_5_out, or_2_out, xor_3_out);
  and and_6 (and_6_out, A[2], not_3_out);
  xor xor_10 (R[3], xor_4_out, or_3_out);
  and and_7 (and_7_out, or_3_out, xor_4_out);
  and and_8 (and_8_out, A[3], not_4_out);
  xor xor_11 (R[4], xor_5_out, or_4_out);
  and and_9 (and_9_out, or_4_out, xor_5_out);
  and and_10 (and_10_out, A[4], not_5_out);
  xor xor_12 (R[5], xor_6_out, or_5_out);
  and and_11 (and_11_out, or_5_out, xor_6_out);
  and and_12 (and_12_out, A[5], not_6_out);
  or or_1 (or_1_out, and_1_out, and_2_out);
  or or_2 (or_2_out, and_3_out, and_4_out);
  or or_3 (or_3_out, and_5_out, and_6_out);
  or or_4 (or_4_out, and_7_out, and_8_out);
  or or_5 (or_5_out, and_9_out, and_10_out);
  or or_6 (C_out, and_11_out, and_12_out);
  xor xor_13 (V, or_5_out, C_out);
  // Probe on R
endmodule

module one_bit_adder (
  input  A,
  input  B,
  input  C_in,
  output SUM,
  output C_out
);

  wire and_1_out, and_2_out, and_3_out;

  and and_1 (and_1_out, A, B);
  and and_2 (and_2_out, C_in, B);
  and and_3 (and_3_out, A, C_in);
  xor xor_1 (SUM, A, B, C_in);
  or or_1 (C_out, and_1_out, and_2_out, and_3_out);
endmodule
