// Logisim project 7COM1013.circ-T02L1e05.circ as structural Verilog: 1 circuit, main circuit solution
module solution (
  input  [3:0] A,
  output [5:0] R
);

  assign R = {{2{A[3]}}, A};  // Bit_Extender bit_extender_1
endmodule
