// Logisim project 7COM1013.circ-T02L1e06.circ as structural Verilog: 1 circuit, main circuit solution
module solution (
  input  [1:0] A,
  input  E,
  output R0,
  output R1,
  output R2,
  output R3
);

  wire not_1_out, not_2_out;

  not not_1 (not_1_out, A[0]);
  not not_2 (not_2_out, A[1]);
  and and_1 (R0, E, not_1_out, not_2_out);
  and and_2 (R1, E, A[0], not_2_out);
  and and_3 (R2, not_1_out, E, A[1]);
  and and_4 (R3, A[0], E, A[1]);
endmodule
