// Logisim project 7COM1013.circ-T02L1e07.circ as structural Verilog: 1 circuit, main circuit solution
module solution (
  input  [5:0] A,
  output [5:0] R
);

  wire not_1_out, xor_1_out;

  not not_1 (not_1_out, xor_1_out);
  xor xor_1 (xor_1_out, A[3], A[2]);
  xor xor_2 (R[5], A[5], not_1_out);

  assign R[4:0] = A[4:0];
endmodule
