// Logisim project 7COM1013.circ-T02L1e08.circ as structural Verilog: 2 circuits, main circuit solution
module _2_to_4 (
  input  [1:0] A,
  input  E,
  output R0,
  output R1,
  output R2,
  output R3
);

  and and_1 (R0, ~A[0], ~A[1], E);  // AND_Gate
  and and_2 (R1, A[0], ~A[1], E);  // AND_Gate
  and and_3 (R2, ~A[0], A[1], E);  // AND_Gate
  and and_4 (R3, A[0], A[1], E);
endmodule

module solution (
  input  [3:0] A,
  input  E,
  output R0,
  output R1,
  output R2,
  output R3,
  output R4,
  output R5,
  output R6,
  output R7,
  output R8,
  output R9,
  output R10,
  output R11,
  output R12,
  output R13,
  output R14,
  output R15
);

  wire and_1_out, and_2_out, and_3_out, and_4_out, not_1_out, not_2_out, not_3_out, not_4_out;

  not not_1 (not_1_out, A[2]);
  not not_2 (not_2_out, A[3]);
  and and_1 (and_1_out, E, not_1_out, not_2_out);
  and and_2 (and_2_out, E, A[2], not_2_out);
  and and_3 (and_3_out, not_1_out, E, A[3]);
  and and_4 (and_4_out, A[2], E, A[3]);
  not not_3 (not_3_out, A[0]);
  not not_4 (not_4_out, A[1]);
  and and_5 (R0, and_1_out, not_3_out, not_4_out);
  and and_6 (R1, and_1_out, A[0], not_4_out);
  and and_7 (R2, not_3_out, and_1_out, A[1]);
  and and_8 (R3, A[0], and_1_out, A[1]);
  and and_9 (R4, and_2_out, not_3_out, not_4_out);
  and and_10 (R5, and_2_out, A[0], not_4_out);
  and and_11 (R6, not_3_out, and_2_out, A[1]);
  and and_12 (R7, A[0], and_2_out, A[1]);
  and and_13 (R8, and_3_out, not_3_out, not_4_out);
  and and_14 (R9, and_3_out, A[0], not_4_out);
  and and_15 (R10, not_3_out, and_3_out, A[1]);
  and and_16 (R11, A[0], and_3_out, A[1]);
  and and_17 (R12, and_4_out, not_3_out, not_4_out);
  and and_18 (R13, and_4_out, A[0], not_4_out);
  and and_19 (R14, not_3_out, and_4_out, A[1]);
  and and_20 (R15, A[0], and_4_out, A[1]);
endmodule
