// Logisim project 7COM1013.circ-T02L1e09.circ as structural Verilog: 1 circuit, main circuit solution
module solution (
  input  [5:0] A,
  input  [5:0] B,
  output [5:0] R
);

  wire comparator_1_eq, comparator_1_gt, or_1_out;
  wire [5:0] adder_1_out, and_1_out, and_2_out, bit_extender_1_out, bit_extender_2_out, not_1_out, not_2_out,
       subtractor_1_out;

  // Probe on A
  // Probe on B
  Comparator #(.width(6)) comparator_1 (.a(A), .b(B), .gt(comparator_1_gt), .eq(comparator_1_eq));  // open: lt
  Subtractor #(.width(6)) subtractor_1 (.a(A), .b(B), .out(subtractor_1_out));  // open: bin, bout
  assign not_1_out = ~subtractor_1_out;  // NOT_Gate not_1, 6 bits wide
  assign bit_extender_1_out = {{5{1'b0}}, 1'b1};  // Bit_Extender bit_extender_1
  or or_1 (or_1_out, comparator_1_gt, comparator_1_eq);
  Adder #(.width(6)) adder_1 (.a(not_1_out), .b(bit_extender_1_out), .out(adder_1_out));  // open: cin, cout
  assign not_2_out = ~bit_extender_2_out;  // NOT_Gate not_2, 6 bits wide
  assign bit_extender_2_out = {{5{or_1_out}}, or_1_out};  // Bit_Extender bit_extender_2
  assign and_1_out = subtractor_1_out & bit_extender_2_out;  // AND_Gate and_1, 6 bits wide
  assign and_2_out = adder_1_out & not_2_out;  // AND_Gate and_2, 6 bits wide
  assign R = and_1_out | and_2_out;  // OR_Gate or_2, 6 bits wide
  // Probe on R
endmodule
