// Logisim project 7COM1013.circ-T03L1e03.circ as structural Verilog: 1 circuit, main circuit solution
module solution (
  input  In1,
  input  In2,
  input  In3,
  output Out
);

  wire and_1_out, and_2_out, and_3_out, not_1_out, not_2_out, not_3_out, not_4_out, not_5_out, not_6_out;

  not not_1 (not_1_out, In1);
  not not_2 (not_2_out, In2);
  not not_3 (not_3_out, In1);
  not not_4 (not_4_out, In3);
  not not_5 (not_5_out, In2);
  not not_6 (not_6_out, In3);
  and and_1 (and_1_out, not_1_out, not_2_out);
  and and_2 (and_2_out, not_3_out, not_4_out);
  and and_3 (and_3_out, not_5_out, not_6_out);
  or or_1 (Out, and_1_out, and_2_out, and_3_out);
endmodule
