// Logisim project 7COM1013.circ-T04L1e01.circ as structural Verilog: 1 circuit, main circuit solution
module solution (
  input  [3:0] INDATA,
  input  Load,
  input  Enable,
  input  ClocK,
  output [3:0] OUTDATA
);

  wire [3:0] adder_1_out, multiplexer_1_out;

  // Probe on adder_1_out
  Adder #(.width(4)) adder_1 (.a(4'b0001), .b(OUTDATA), .out(adder_1_out));  // open: cin, cout
  // Probe on multiplexer_1_out
  Multiplexer #(.width(4)) multiplexer_1 (
    .in0(adder_1_out), .in1(INDATA), .out(multiplexer_1_out), .sel(Load));  // open: en
  // Probe on OUTDATA
  Register #(.width(4), .trigger("falling")) register_1 (
    .D(multiplexer_1_out), .en(Enable), .Q(OUTDATA), .clk(ClocK));  // open: clr
endmodule
