// Logisim project 7COM1013.circ-T04L1e02.circ as structural Verilog: 1 circuit, main circuit solution
module solution (
  input  [3:0] INDATA,
  input  Load,
  input  Enable,
  input  ClocK,
  output [3:0] OUTDATA
);

  wire adder_1_cout;
  wire [3:0] adder_1_out, multiplexer_1_out;
  wire [3:3] register_1_q;

  Register #(.width(1)) register_1 (.D(adder_1_cout), .en(Enable), .Q(register_1_q[3]), .clk(ClocK));  // open: clr
  Adder #(.width(4)) adder_1 (
    .a(OUTDATA), .b({{3{register_1_q[3]}}, 1'b0}), .out(adder_1_out), .cin(1'b1), .cout(adder_1_cout));
  Multiplexer #(.width(4)) multiplexer_1 (
    .in0(adder_1_out), .in1(INDATA), .out(multiplexer_1_out), .sel(Load));  // open: en
  // Probe on multiplexer_1_out
  Register #(.width(4), .trigger("falling")) register_2 (
    .D(multiplexer_1_out), .en(Enable), .Q(OUTDATA), .clk(ClocK));  // open: clr
endmodule
