// Logisim project 7COM1013.circ-T04L1e03.circ as structural Verilog: 1 circuit, main circuit solution
module solution (
  input  Reset,
  input  Clock,
  output [10:0] garland
);

  wire [10:0] multiplexer_1_out;
  wire [10:10] not_1_out;

  not not_1 (not_1_out[10], Reset);
  Multiplexer #(.width(11)) multiplexer_1 (
    .in0({garland[9:0], garland[10]}), .in1({{5{not_1_out[10]}}, Reset, {5{not_1_out[10]}}}),
    .out(multiplexer_1_out), .sel(Reset));  // open: en
  Register #(.width(11), .trigger("falling")) register_1 (
    .D(multiplexer_1_out), .en(1'b1), .Q(garland), .clk(Clock));  // open: clr
  DotMatrix #(.matrixcols(1), .matrixrows(11)) dotmatrix_1 (.col0(garland));
endmodule
