// Logisim project 7COM1013.circ-T04L1e04.circ as structural Verilog: 1 circuit, main circuit solution
module solution (
  input  Reset,
  input  Clock,
  output [10:0] out_3
);

  wire or_1_out, or_2_out, register_1_q, xor_1_out;
  wire [10:0] multiplexer_1_out, multiplexer_2_out;
  wire [10:10] not_1_out;

  Register #(.width(1), .trigger("falling")) register_1 (
    .D(xor_1_out), .en(1'b1), .Q(register_1_q), .clk(Clock));  // open: clr
  xor xor_1 (xor_1_out, out_3[1], or_1_out);
  or or_1 (or_1_out, out_3[1], or_2_out);
  or or_2 (or_2_out, register_1_q, out_3[10]);
  not not_1 (not_1_out[10], Reset);
  Multiplexer #(.width(11)) multiplexer_1 (
    .in0({out_3[9:0], out_3[10]}), .in1({out_3[0], out_3[10:1]}), .out(multiplexer_1_out), .sel(or_2_out));  // open: en
  Multiplexer #(.width(11)) multiplexer_2 (
    .in0(multiplexer_1_out), .in1({{5{not_1_out[10]}}, Reset, {5{not_1_out[10]}}}), .out(multiplexer_2_out),
    .sel(Reset));  // open: en
  Register #(.width(11), .trigger("falling")) register_2 (
    .D(multiplexer_2_out), .en(1'b1), .Q(out_3), .clk(Clock));  // open: clr
  DotMatrix #(.inputtype("row"), .matrixcols(11), .matrixrows(1)) dotmatrix_1 (.row0(out_3));
endmodule
