// Logisim project 7COM1013.circ-T04L1e05.circ as structural Verilog: 1 circuit, main circuit solution
module solution (
  input  [5:0] Target,
  input  Load,
  input  Clock,
  output Stop,
  output [4:0] Location,
  output Found
);

  wire or_1_out;
  wire [4:0] bit_extender_1_out;
  wire [5:0] rom_1_data;
  wire [7:0] adder_1_out, address_q, bit_extender_2_out, bit_extender_3_out, multiplexer_1_out, target_q;

  Multiplexer #(.width(8)) multiplexer_1 (
    .in0(adder_1_out), .in1(8'h1), .out(multiplexer_1_out), .sel(Load));  // open: en
  Register #(.trigger("falling")) address (.D(multiplexer_1_out), .Q(address_q), .clk(Clock));  // open: en, clr
  Bit_Extender #(.out_width(5)) bit_extender_1 (.in(address_q), .out(bit_extender_1_out));
  Adder adder_1 (.a(8'h1), .b(address_q), .out(adder_1_out), .cin(1'b0));  // open: cout
  assign bit_extender_2_out = {{2{1'b0}}, Target};  // Bit_Extender bit_extender_2
  Register #(.trigger("falling")) u_target (.D(bit_extender_2_out), .en(Load), .Q(target_q), .clk(Clock));  // open: clr
  ROM #(.addrWidth(5), .dataWidth(6)) rom_1 (.addr(bit_extender_1_out), .data(rom_1_data));  // open: sel
  Comparator comparator_1 (.a(target_q), .b(bit_extender_3_out), .eq(Found));  // open: gt, lt
  assign bit_extender_3_out = {{2{1'b0}}, rom_1_data};  // Bit_Extender bit_extender_3
  Comparator #(.width(5)) comparator_2 (.a({5{1'b1}}), .b(bit_extender_1_out), .eq(Stop));  // open: gt, lt
  assign Location = or_1_out ? bit_extender_1_out : 5'bz;  // Controlled_Buffer controlled_buffer_1
  or or_1 (or_1_out, Found, Stop);

  // Other names for the same wires on the sheet: clk = Clock

  // Notes on the sheet:
  //   contents of rom_1 (hex, n*v repeats v):
  //   24 c 1b 2d 28 3d 38 14 3b 1c 29 36 1c 2e 7 3a 35 31 3d 15 a 37 34 a c c 2a 32 17 11 12 29
endmodule
