// Logisim project 7COM1013.circ-T04L1e06.circ as structural Verilog: 1 circuit, main circuit fib32
module fib32 (
  input  clock,
  output [31:0] a,
  output [5:0] k,
  output stop
);

  wire comparator_1_eq;
  wire [5:0] adder_2_out;
  wire [31:0] A_2_q, A_q, adder_1_out, multiplexer_1_out;

  Multiplexer #(.width(32)) multiplexer_1 (
    .in0(adder_1_out), .in1(32'h1), .out(multiplexer_1_out), .sel(comparator_1_eq));  // open: en
  // Probe on A_q
  Register #(.width(32)) u_A (.D(multiplexer_1_out), .Q(A_q), .clk(clock));  // open: en, clr
  Comparator #(.width(6)) comparator_1 (.a({6{1'b0}}), .b(k), .eq(comparator_1_eq));  // open: gt, lt
  // Probe on A_2_q
  Register #(.width(32)) A_2 (.D(a), .Q(A_2_q), .clk(clock));  // open: en, clr
  Register #(.width(32), .trigger("falling")) B (.D(A_q), .Q(a), .clk(clock));  // open: en, clr
  // Probe on adder_1_out
  Adder #(.width(32)) adder_1 (.a(A_2_q), .b(a), .out(adder_1_out), .cin(1'b0));  // open: cout
  // Probe on a
  // Probe on a
  Register #(.width(6), .trigger("falling")) A_3 (.D(adder_2_out), .Q(k), .clk(clock));  // open: en, clr
  // Probe on k
  Adder #(.width(6)) adder_2 (.a(6'b000001), .b(k), .out(adder_2_out), .cin(1'b0));  // open: cout
  Comparator #(.width(32)) comparator_2 (.a(a), .b({32{1'b1}}), .lt(stop));  // open: gt, eq

  // Other names for the same wires on the sheet: Clk = clock
endmodule
