// Logisim project 7COM1013.circ-T04L1e07.circ as structural Verilog: 2 circuits, main circuit solution
module solution (
  input  [7:0] A,
  input  set,
  input  [7:0] B,
  input  clock,
  output [7:0] GCD,
  output done
);

  wire comparator_1_gt, comparator_1_lt;
  wire [7:0] A_q, B_q, multiplexer_1_out, multiplexer_2_out, multiplexer_3_out, multiplexer_4_out,
       subtractor_1_out, subtractor_2_out;

  // Probe on A
  // Probe on B
  Register u_A (.D(multiplexer_1_out), .Q(A_q), .clk(clock));  // open: en, clr
  Multiplexer #(.width(8)) multiplexer_1 (
    .in0(multiplexer_3_out), .in1(A), .out(multiplexer_1_out), .sel(set));  // open: en
  Multiplexer #(.width(8)) multiplexer_2 (
    .in0(multiplexer_4_out), .in1(B), .out(multiplexer_2_out), .sel(set));  // open: en
  Register u_B (.D(multiplexer_2_out), .Q(B_q), .clk(clock));  // open: en, clr
  Multiplexer #(.width(8)) multiplexer_3 (
    .in0(A_q), .in1(subtractor_1_out), .out(multiplexer_3_out), .sel(comparator_1_gt));  // open: en
  Comparator comparator_1 (.a(A_q), .b(B_q), .gt(comparator_1_gt), .eq(done), .lt(comparator_1_lt));
  Subtractor subtractor_1 (.a(A_q), .b(B_q), .out(subtractor_1_out));  // open: bin, bout
  Subtractor subtractor_2 (.a(B_q), .b(A_q), .out(subtractor_2_out));  // open: bin, bout
  Multiplexer #(.width(8)) multiplexer_4 (
    .in0(B_q), .in1(subtractor_2_out), .out(multiplexer_4_out), .sel(comparator_1_lt));  // open: en
  assign GCD = done ? A_q : 8'bz;  // Controlled_Buffer controlled_buffer_1
  // Probe on GCD

  // Other names for the same wires on the sheet: Clk = clock
endmodule

module stopper (
  input  run_prime,
  input  stop,
  input  clock_in,
  output clock_out
);

  wire multiplexer_1_out, not_1_out, or_1_out, register_1_q;

  not not_1 (not_1_out, stop);
  Multiplexer #(.enable("false")) multiplexer_1 (
    .in0(not_1_out), .in1(run_prime), .out(multiplexer_1_out), .sel(run_prime));
  or or_1 (or_1_out, run_prime, register_1_q);
  Register #(.width(1), .trigger("falling")) register_1 (
    .D(multiplexer_1_out), .en(or_1_out), .Q(register_1_q), .clk(clock_in));  // open: clr
  and and_1 (clock_out, register_1_q, clock_in);
endmodule
